# Fritzing sketch water_filter_board (saved by Fritzing 0.9.3b)
perfboards: 2

parts:
  S6 = Load Sensor - 50kg [part_number=SEN-10245]
  S7 = Load Sensor - 50kg [part_number=SEN-10245]
  S8 = Load Sensor - 50kg [part_number=SEN-10245]
  S9 = Load Sensor - 50kg [part_number=SEN-10245]
  J1 = female pin header, 3 pins [form="♀ (female)"]
  J2 = female pin header, 3 pins [form="♀ (female)"]
  J3 = female pin header, 3 pins [form="♀ (female)"]
  J4 = female pin header, 3 pins [form="♀ (female)"]
  J5 = female pin header, 4 pins [form="♀ (female)"]
  Part2 = HX711 Weighing Sensor Module  # not connected
  J6 = female pin header, 6 pins [form="♀ (female)"]
  U1 = NodeMCU V3.0
  J7 = female pin header, 4 pins [form="♀ (female)"]
  J8 = female pin header, 4 pins [form="♀ (female)"]  # not connected
  J9 = female pin header, 4 pins [form="♀ (female)"]
  J10 = female pin header, 4 pins [form="♀ (female)"]  # not connected
  J11 = female pin header, 15 pins [form="♀ (female)"]
  J12 = female pin header, 15 pins [form="♀ (female)"]
  Grove1 = Grove OLED 128x96
  J13 = female pin header, 4 pins [form="♀ (female)"]

nets:
  N1: S6.B, S8.B, J1.pin1, J2.pin3
  N2: S6.W, S9.W, J2.pin1, J3.pin3
  N3: S6.R, J2.pin2, J6.pin1
  N4: S7.B, S9.B, J3.pin1, J4.pin3
  N5: S7.W, S8.W, J1.pin3, J4.pin1
  N6: S8.R, J1.pin2
  N7: S9.R, J3.pin2, J6.pin3
  N8: J4.pin2, J6.pin2
  N9: J5.pin1, J7.pin1
  N10: J5.pin2, J7.pin2
  N11: J5.pin3, J7.pin3
  N12: J5.pin4, J7.pin4
  N13: U1.GND#6, U1.GND#13, U1.GND#16, U1.GND#33
  N14: J9.pin1, J11.pin7
  N15: J9.pin2, J11.pin8
  N16: J9.pin3, J11.pin9
  N17: J9.pin4, J11.pin15
  N18: J11.pin2, Grove1.SCL, J13.pin2
  N19: J11.pin3, Grove1.SDA, J13.pin1
  N20: J12.pin2, Grove1.GND, J13.pin4
  N21: J12.pin11, Grove1.VCC, J13.pin3

notes:
  1
  2
  3
  4
  E+ E- A- A+
  Same orientation
  as on the breadboard
  Second board mounted on top of first

custom parts:
  Load Sensor - 50kg: Half-wheatstone bridge Load Cell modified from the Fritzing Repo This load sensor, sometimes called a strain gauge, is the same one found in digital bathroom scales (you know, the ones you use in January for your New Year's resolutions, and then forget about a month later). This sensor can measure up to about 110 pounds.
  NodeMCU V3.0: ESP8266 based NodeMCU
