# Fritzing sketch tinyscreen (saved by Fritzing 0.9.3b)

parts:
  Part1 = Arduino Nano (Rev3.0) (ICSP)
  Grove1 = Grove OLED 128x96

nets:
  GND: Part1.GND, Grove1.GND
  N1: Part1.A5, Grove1.SCL
  N2: Part1.A4, Grove1.SDA
  3V3: Part1.3V3, Grove1.VCC
