# Fritzing sketch water-filter (saved by Fritzing 0.9.3b)
perfboards: 1

parts:
  LED2 = RGB LED (com. cathode, rgb) [package="5 mm [THT]"]
  Part4 = HX711 Weighing Sensor Module
  Load_Cell1 = Load Cell - Red/white/black/green
  U1 = NodeMCU V3.0
  J1 = female pin header, 4 pins [form="♀ (female)"]
  J2 = female pin header, 15 pins [form="♀ (female)"]
  J3 = female pin header, 15 pins [form="♀ (female)"]  # not connected
  J4 = female pin header, 6 pins [form="♀ (female)"]
  J5 = male pin header, 6 pins [form="♂ (male)"]
  J6 = male pin header, 4 pins [form="♂ (male)"]
  U2 = NodeMCU V3.0  # not connected

nets:
  N1: LED2.red_anode, U1.D8
  GND: LED2.common_cathode, Part4.GND, U1.GND
  N2: LED2.green_anode, U1.D6
  N3: LED2.blue_anode, U1.D5
  VCC: Part4.VCC, U1.3V3
  N4: Part4.DO/RX, U1.D2
  N5: Part4.CK/TX, U1.D3
  N6: Part4.E+, Load_Cell1.wire1
  N7: Part4.E-, Load_Cell1.wire3
  N8: Part4.A+, Load_Cell1.wire4
  N9: Part4.A-, Load_Cell1.wire2
  N10: J1.pin1, J2.pin2
  N11: J1.pin2, J2.pin13
  N12: J1.pin3, J2.pin12
  N13: J1.pin4, J2.pin10
  N14: J2.pin5, J6.pin1
  N15: J2.pin7, J6.pin2
  N16: J2.pin8, J6.pin3
  N17: J2.pin9, J6.pin4
  N18: J4.pin1, J5.pin1
  N19: J4.pin2, J5.pin2
  N20: J4.pin3, J5.pin3
  N21: J4.pin4, J5.pin4

custom parts:
  Load Cell - Red/white/black/green: A rectangle load cell/weighting pressure Sensor with four wires - Red, white, black, green. Normally corresponding with E+, E-, A+, A- respectively.
  NodeMCU V3.0: ESP8266 based NodeMCU
